# Fritzing sketch L298N_UNO (saved by Fritzing 0.9.3b)
breadboards: 1

parts:
  Parça1 = Arduino Uno (Rev3)
  S1 = H-Bridge with L298N
  M1 = DC Motor
  M2 = DC Motor
  VCC1 = Battery block 9V

nets:
  N1: Parça1.D9_PWM, S1.ENA
  N2: Parça1.D3_PWM, S1.ENB
  N3: Parça1.D4, S1.IN4
  N4: Parça1.D5_PWM, S1.IN3
  N5: Parça1.D6_PWM, S1.IN2
  N6: Parça1.D7, S1.IN1
  GND: Parça1.GND, S1.GND, VCC1.-
  N7: S1.12V, VCC1.+
  N8: S1.M1-01, M1.pin_2
  N9: S1.M1-02, M1.pin_1
  N10: S1.M2-01, M2.pin_2
  N11: S1.M2-02, M2.pin_1

custom parts:
  H-Bridge with L298N: h-bridge
